// Logisim project ETFStudent.circ as structural Verilog: 14 circuits, main circuit REG32_LD
module REG32_LD (
  input  [31:0] I15__0,
  input  LD,
  input  mr,
  input  CLK,
  output [31:0] A15__0
);

  // REG16_LD reg16_ld_1: pin names not known; wires that end beside it: CLK, mr, I15__0[31:16], A15__0[31:16], LD
  // REG16_LD reg16_ld_2: pin names not known; wires that end beside it: CLK, mr, I15__0[15:0], A15__0[15:0], LD

  // Notes on the sheet:
  //   __
endmodule

module KMADR (
  input  immed,
  input  memind,
  input  regdir,
  input  regind,
  input  predec,
  input  pcrelpom,
  output [4:0] Adr4__0
);

  assign Adr4__0 = immed ? 5'b00010 : 5'bz;  // Controlled_Buffer controlled_buffer_1
  assign Adr4__0 = memind ? 5'b00011 : 5'bz;  // Controlled_Buffer controlled_buffer_2
  assign Adr4__0 = regdir ? 5'b01001 : 5'bz;  // Controlled_Buffer controlled_buffer_3
  assign Adr4__0 = regind ? 5'b01011 : 5'bz;  // Controlled_Buffer controlled_buffer_4
  assign Adr4__0 = predec ? 5'b01100 : 5'bz;  // Controlled_Buffer controlled_buffer_5
  assign Adr4__0 = pcrelpom ? 5'b10000 : 5'bz;  // Controlled_Buffer controlled_buffer_6
endmodule

module KMOPR (
  input  HALT,
  input  RTS,
  input  RTI,
  input  ROR,
  input  PUSH,
  input  POP,
  input  BOVF,
  input  BNCR,
  input  BLEQ,
  input  BLSSU,
  input  JLEQ,
  input  JMP,
  input  JSR,
  input  LD,
  input  ST,
  input  DEC,
  input  SUB,
  input  XOR,
  input  AND,
  input  STRFIND,
  output [6:0] Adr6__0
);

  assign Adr6__0 = HALT ? 7'b0000010 : 7'bz;  // Controlled_Buffer controlled_buffer_1
  assign Adr6__0 = RTS ? 7'b0000011 : 7'bz;  // Controlled_Buffer controlled_buffer_2
  assign Adr6__0 = RTI ? 7'b0001001 : 7'bz;  // Controlled_Buffer controlled_buffer_3
  assign Adr6__0 = ROR ? 7'b0010010 : 7'bz;  // Controlled_Buffer controlled_buffer_4
  assign Adr6__0 = PUSH ? 7'b0010100 : 7'bz;  // Controlled_Buffer controlled_buffer_5
  assign Adr6__0 = POP ? 7'b0011010 : 7'bz;  // Controlled_Buffer controlled_buffer_6
  assign Adr6__0 = BOVF ? 7'b0100000 : 7'bz;  // Controlled_Buffer controlled_buffer_7
  assign Adr6__0 = BNCR ? 7'b0100000 : 7'bz;  // Controlled_Buffer controlled_buffer_8
  assign Adr6__0 = BLEQ ? 7'b0100000 : 7'bz;  // Controlled_Buffer controlled_buffer_9
  assign Adr6__0 = BLSSU ? 7'b0100000 : 7'bz;  // Controlled_Buffer controlled_buffer_10
  assign Adr6__0 = JLEQ ? 7'b0100010 : 7'bz;  // Controlled_Buffer controlled_buffer_11
  assign Adr6__0 = JMP ? 7'b0100011 : 7'bz;  // Controlled_Buffer controlled_buffer_12
  assign Adr6__0 = JSR ? 7'b0100100 : 7'bz;  // Controlled_Buffer controlled_buffer_13
  assign Adr6__0 = LD ? 7'b0101010 : 7'bz;  // Controlled_Buffer controlled_buffer_14
  assign Adr6__0 = ST ? 7'b0101100 : 7'bz;  // Controlled_Buffer controlled_buffer_15
  assign Adr6__0 = SUB ? 7'b0111010 : 7'bz;  // Controlled_Buffer controlled_buffer_16
  assign Adr6__0 = DEC ? 7'b0110011 : 7'bz;  // Controlled_Buffer controlled_buffer_17
  assign Adr6__0 = XOR ? 7'b0111100 : 7'bz;  // Controlled_Buffer controlled_buffer_18
  assign Adr6__0 = AND ? 7'b0111110 : 7'bz;  // Controlled_Buffer controlled_buffer_19
  assign Adr6__0 = STRFIND ? 7'b1000000 : 7'bz;  // Controlled_Buffer controlled_buffer_20
endmodule

module REG6_INC_LD (
  input  [5:0] I5__0,
  input  LD,
  input  INC,
  input  mr,
  input  CLK,
  output [5:0] A5__0
);

  wire reg2m_inc_ld_1_p7, reg2m_inc_ld_2_p8;

  // REG2m_INC_LD reg2m_inc_ld_1: pin names not known; wires that end beside it: CLK, mr, I5__0[5:4], A5__0[5:4], LD, INC, reg2m_inc_ld_1_p7
  // REG2m_INC_LD reg2m_inc_ld_2: pin names not known; wires that end beside it: CLK, reg2m_inc_ld_1_p7, mr, I5__0[3:2], A5__0[3:2], LD, INC, reg2m_inc_ld_2_p8
  // REG2m_INC_LD reg2m_inc_ld_3: pin names not known; wires that end beside it: CLK, reg2m_inc_ld_2_p8, mr, I5__0[1:0], A5__0[1:0], LD, INC, INC

  // Notes on the sheet:
  //   __
endmodule

module ROM32x24_FETCH (
  input  [4:0] A4__0,
  input  CS,
  output [23:0] DOUT
);

  ROM #(.addrWidth(5), .dataWidth(24)) rom_1 (.addr(A4__0), .data(DOUT), .sel(CS));
endmodule

module MP2_5b (
  input  En,
  input  [4:0] in_2,
  input  [4:0] in_3,
  input  S0,
  output [4:0] Y
);

  wire not_1_out;
  wire [4:0] and_1_out, and_2_out, bit_extender_1_out, bit_extender_2_out, bit_extender_3_out, or_1_out;

  Pull_Resistor #(.pull(1)) pull_resistor_1 (.node(En));
  assign bit_extender_1_out = {{4{S0}}, S0};  // Bit_Extender bit_extender_1
  not not_1 (not_1_out, S0);
  assign bit_extender_2_out = {{4{not_1_out}}, not_1_out};  // Bit_Extender bit_extender_2
  assign and_1_out = in_2 & bit_extender_2_out;  // AND_Gate and_1, 5 bits wide
  assign and_2_out = in_3 & bit_extender_1_out;  // AND_Gate and_2, 5 bits wide
  assign bit_extender_3_out = {{4{En}}, En};  // Bit_Extender bit_extender_3
  assign or_1_out = and_1_out | and_2_out;  // OR_Gate or_1, 5 bits wide
  assign Y = bit_extender_3_out & or_1_out;  // AND_Gate and_3, 5 bits wide

  // Notes on the sheet:
  //   I0
  //   4..0
  //   I1
  //   4..0
  //   Ako En nije priključen (stanje visoke impednase - HiZ),
  //   uezti za podrazumevanu vrednost logičku jedinicu
  //   4..0
endmodule

module ROM32x24_ADDR (
  input  [4:0] A4__0,
  input  CS,
  output [23:0] DOUT
);

  ROM #(.addrWidth(5), .dataWidth(24)) rom_1 (.addr(A4__0), .data(DOUT), .sel(CS));
endmodule

module ALU16_SUB_XOR_AND (
  input  Cin,
  input  [15:0] A,
  input  [15:0] B,
  input  sub,
  input  \xor ,
  input  \and ,
  output [15:0] F,
  output Cout
);

  wire subtractor_1_bout;
  wire [15:0] and_1_out, subtractor_1_out, xor_1_out;

  Subtractor #(.width(16)) subtractor_1 (.a(A), .b(B), .out(subtractor_1_out), .bin(Cin), .bout(subtractor_1_bout));
  assign xor_1_out = A ^ B;  // XOR_Gate xor_1, 16 bits wide
  assign and_1_out = A & B;  // AND_Gate and_1, 16 bits wide
  assign F = sub ? subtractor_1_out : 16'bz;  // Controlled_Buffer controlled_buffer_1
  assign Cout = sub ? subtractor_1_bout : 1'bz;  // Controlled_Buffer controlled_buffer_2
  assign F = \xor  ? xor_1_out : 16'bz;  // Controlled_Buffer controlled_buffer_3
  assign F = \and  ? and_1_out : 16'bz;  // Controlled_Buffer controlled_buffer_4
endmodule

module ROM128x52 (
  input  [6:0] A5__0,
  input  CS,
  output [31:0] DOUT31__0,
  output [19:0] DOUT51__32
);

  ROM #(.addrWidth(7), .dataWidth(20)) rom_1 (.addr(A5__0), .data(DOUT51__32), .sel(CS));
  ROM #(.addrWidth(7), .dataWidth(32)) rom_2 (.addr(A5__0), .data(DOUT31__0), .sel(CS));
endmodule

module REG7_INC_LD (
  input  [6:0] I6__0,
  input  LD,
  input  INC,
  input  mr,
  input  CLK,
  output [6:0] A6__0
);

  wire reg1m_inc_ld_1_p7, reg2m_inc_ld_1_p8, reg2m_inc_ld_2_p9;

  // REG1m_INC_LD reg1m_inc_ld_1: pin names not known; wires that end beside it: CLK, mr, I6__0[6], A6__0[6], LD, INC, reg1m_inc_ld_1_p7
  // REG2m_INC_LD reg2m_inc_ld_1: pin names not known; wires that end beside it: CLK, reg1m_inc_ld_1_p7, mr, I6__0[5:4], A6__0[5:4], LD, INC, reg2m_inc_ld_1_p8
  // REG2m_INC_LD reg2m_inc_ld_2: pin names not known; wires that end beside it: CLK, reg2m_inc_ld_1_p8, mr, A6__0[5:4], I6__0[3:2], A6__0[3:2], LD, INC, reg2m_inc_ld_2_p9
  // REG2m_INC_LD reg2m_inc_ld_3: pin names not known; wires that end beside it: CLK, reg2m_inc_ld_2_p9, mr, I6__0[1:0], A6__0[1:0], LD, INC, INC

  // Notes on the sheet:
  //   __
endmodule

module MP2_7b (
  input  En,
  input  [6:0] _6__0,
  input  [6:0] in_3,
  input  S0,
  output [6:0] Y
);

  wire not_1_out;
  wire [6:0] and_1_out, and_2_out, bit_extender_1_out, bit_extender_2_out, bit_extender_3_out, or_1_out;

  Pull_Resistor #(.pull(1)) pull_resistor_1 (.node(En));
  assign bit_extender_1_out = {{6{S0}}, S0};  // Bit_Extender bit_extender_1
  not not_1 (not_1_out, S0);
  assign bit_extender_2_out = {{6{not_1_out}}, not_1_out};  // Bit_Extender bit_extender_2
  assign and_1_out = _6__0 & bit_extender_2_out;  // AND_Gate and_1, 7 bits wide
  assign and_2_out = in_3 & bit_extender_1_out;  // AND_Gate and_2, 7 bits wide
  assign bit_extender_3_out = {{6{En}}, En};  // Bit_Extender bit_extender_3
  assign or_1_out = and_1_out | and_2_out;  // OR_Gate or_1, 7 bits wide
  assign Y = bit_extender_3_out & or_1_out;  // AND_Gate and_3, 7 bits wide

  // Notes on the sheet:
  //   I0
  //   I1
  //   6..0
  //   Ako En nije priključen (stanje visoke impednase - HiZ),
  //   uezti za podrazumevanu vrednost logičku jedinicu
  //   6..0
endmodule

module MP16_8b (
  input  [7:0] I0,
  input  [7:0] I1,
  input  [7:0] I2,
  input  [7:0] I3,
  input  [7:0] I4,
  input  [7:0] I5,
  input  [7:0] I6,
  input  [7:0] I7,
  input  S3,
  input  S2,
  input  S1,
  input  S0,
  input  [7:0] I8,
  input  [7:0] I9,
  input  [7:0] I10,
  input  [7:0] I11,
  input  [7:0] I12,
  input  [7:0] I13,
  input  [7:0] I14,
  input  [7:0] I15,
  output [7:0] Y
);

  wire mp8_8b_1_p8, mp8_8b_2_p8;

  // MP8_8b mp8_8b_1: pin names not known; wires that end beside it: S2, S1, S0, I0, I1, I2, I3, mp8_8b_1_p8, I4, I5, I6, I7, 1'b1
  // MP8_8b mp8_8b_2: pin names not known; wires that end beside it: S2, S1, S0, I8, I9, I10, I11, mp8_8b_2_p8, I12, I13, I14, I15, 1'b1
  // MP2_8b mp2_8b_1: pin names not known; wires that end beside it: S3, mp8_8b_1_p8, Y, mp8_8b_2_p8, 1'b1
endmodule

module ROM32x28 (
  input  [4:0] A4__0,
  input  CS,
  output [27:0] DOUT
);

  ROM #(.addrWidth(5), .dataWidth(28)) rom_1 (.addr(A4__0), .data(DOUT), .sel(CS));
endmodule

module GPR16x16 (
  input  [15:0] DI15__0,
  input  [3:0] A3__0,
  input  WR,
  input  CLK,
  output [15:0] DO15__0
);

  wire and_8_out, CS0, CS1, CS2, CS3, CS4, CS5, CS6, CS7, CS8, CS9, CS10, CS11, CS12, CS13, CS14, CS15,
       reg16_ld_1_p4, reg16_ld_2_p4, reg16_ld_3_p4, reg16_ld_4_p4, reg16_ld_5_p4, reg16_ld_6_p4,
       reg16_ld_7_p4, reg16_ld_9_p4, reg16_ld_10_p4, reg16_ld_11_p4, reg16_ld_12_p4, reg16_ld_13_p4,
       reg16_ld_14_p4, reg16_ld_15_p4, reg16_ld_16_p4;
  wire [15:0] reg16_ld_1_p3, reg16_ld_2_p3, reg16_ld_3_p3, reg16_ld_4_p3, reg16_ld_5_p3, reg16_ld_6_p3,
       reg16_ld_7_p3, reg16_ld_8_p3, reg16_ld_9_p3, reg16_ld_10_p3, reg16_ld_11_p3, reg16_ld_12_p3,
       reg16_ld_13_p3, reg16_ld_14_p3, reg16_ld_15_p3, reg16_ld_16_p3;

  // DC4_16 dc4_16_1: pin names not known; wires that end beside it: A3__0, 1'b1, CS0, CS1, CS2, CS3, CS4, CS5, CS6, CS7, CS8, CS9, CS10, CS11, CS12, CS13, CS14, CS15
  // REG16_LD reg16_ld_1: pin names not known; wires that end beside it: CLK, DI15__0, reg16_ld_1_p3, reg16_ld_1_p4
  assign DO15__0 = CS0 ? reg16_ld_1_p3 : 16'bz;  // Controlled_Buffer controlled_buffer_1
  // REG16_LD reg16_ld_2: pin names not known; wires that end beside it: CLK, DI15__0, reg16_ld_2_p3, reg16_ld_2_p4
  assign DO15__0 = CS1 ? reg16_ld_2_p3 : 16'bz;  // Controlled_Buffer controlled_buffer_2
  // REG16_LD reg16_ld_3: pin names not known; wires that end beside it: CLK, DI15__0, reg16_ld_3_p3, reg16_ld_3_p4
  assign DO15__0 = CS2 ? reg16_ld_3_p3 : 16'bz;  // Controlled_Buffer controlled_buffer_3
  // REG16_LD reg16_ld_4: pin names not known; wires that end beside it: CLK, DI15__0, reg16_ld_4_p3, reg16_ld_4_p4
  assign DO15__0 = CS3 ? reg16_ld_4_p3 : 16'bz;  // Controlled_Buffer controlled_buffer_4
  and and_1 (reg16_ld_1_p4, CS0, WR);
  and and_2 (reg16_ld_2_p4, CS1, WR);
  and and_3 (reg16_ld_3_p4, CS2, WR);
  and and_4 (reg16_ld_4_p4, CS3, WR);
  // REG16_LD reg16_ld_5: pin names not known; wires that end beside it: CLK, DI15__0, reg16_ld_5_p3, reg16_ld_5_p4
  and and_5 (reg16_ld_5_p4, CS4, WR);
  assign DO15__0 = CS4 ? reg16_ld_5_p3 : 16'bz;  // Controlled_Buffer controlled_buffer_5
  // REG16_LD reg16_ld_6: pin names not known; wires that end beside it: CLK, DI15__0, reg16_ld_6_p3, reg16_ld_6_p4
  and and_6 (reg16_ld_6_p4, CS5, WR);
  assign DO15__0 = CS5 ? reg16_ld_6_p3 : 16'bz;  // Controlled_Buffer controlled_buffer_6
  // REG16_LD reg16_ld_7: pin names not known; wires that end beside it: CLK, DI15__0, reg16_ld_7_p3, reg16_ld_7_p4
  and and_7 (reg16_ld_7_p4, CS6, WR);
  assign DO15__0 = CS6 ? reg16_ld_7_p3 : 16'bz;  // Controlled_Buffer controlled_buffer_7
  and and_8 (and_8_out, CS7, WR);
  // REG16_LD reg16_ld_8: pin names not known; wires that end beside it: CLK, DI15__0, reg16_ld_8_p3, and_8_out
  assign DO15__0 = CS7 ? reg16_ld_8_p3 : 16'bz;  // Controlled_Buffer controlled_buffer_8
  // REG16_LD reg16_ld_9: pin names not known; wires that end beside it: CLK, DI15__0, reg16_ld_9_p3, reg16_ld_9_p4
  assign DO15__0 = CS8 ? reg16_ld_9_p3 : 16'bz;  // Controlled_Buffer controlled_buffer_9
  // REG16_LD reg16_ld_10: pin names not known; wires that end beside it: CLK, DI15__0, reg16_ld_10_p3, reg16_ld_10_p4
  assign DO15__0 = CS9 ? reg16_ld_10_p3 : 16'bz;  // Controlled_Buffer controlled_buffer_10
  // REG16_LD reg16_ld_11: pin names not known; wires that end beside it: CLK, DI15__0, reg16_ld_11_p3, reg16_ld_11_p4
  assign DO15__0 = CS10 ? reg16_ld_11_p3 : 16'bz;  // Controlled_Buffer controlled_buffer_11
  // REG16_LD reg16_ld_12: pin names not known; wires that end beside it: CLK, DI15__0, reg16_ld_12_p3, reg16_ld_12_p4
  assign DO15__0 = CS11 ? reg16_ld_12_p3 : 16'bz;  // Controlled_Buffer controlled_buffer_12
  and and_9 (reg16_ld_9_p4, CS8, WR);
  and and_10 (reg16_ld_10_p4, CS9, WR);
  and and_11 (reg16_ld_11_p4, CS10, WR);
  and and_12 (reg16_ld_12_p4, CS11, WR);
  // REG16_LD reg16_ld_13: pin names not known; wires that end beside it: CLK, DI15__0, reg16_ld_13_p3, reg16_ld_13_p4
  assign DO15__0 = CS12 ? reg16_ld_13_p3 : 16'bz;  // Controlled_Buffer controlled_buffer_13
  // REG16_LD reg16_ld_14: pin names not known; wires that end beside it: CLK, DI15__0, reg16_ld_14_p3, reg16_ld_14_p4
  assign DO15__0 = CS13 ? reg16_ld_14_p3 : 16'bz;  // Controlled_Buffer controlled_buffer_14
  // REG16_LD reg16_ld_15: pin names not known; wires that end beside it: CLK, DI15__0, reg16_ld_15_p3, reg16_ld_15_p4
  assign DO15__0 = CS14 ? reg16_ld_15_p3 : 16'bz;  // Controlled_Buffer controlled_buffer_15
  // REG16_LD reg16_ld_16: pin names not known; wires that end beside it: CLK, DI15__0, reg16_ld_16_p3, reg16_ld_16_p4
  assign DO15__0 = CS15 ? reg16_ld_16_p3 : 16'bz;  // Controlled_Buffer controlled_buffer_16
  and and_13 (reg16_ld_13_p4, CS12, WR);
  and and_14 (reg16_ld_14_p4, CS13, WR);
  and and_15 (reg16_ld_15_p4, CS14, WR);
  and and_16 (reg16_ld_16_p4, CS15, WR);

  // Other names for the same wires on the sheet: inREG[15:0] = DI15__0; outREG[15:0] = DO15__0
endmodule
