// Logisim project ORT2Project.circ as structural Verilog: 8 circuits, main circuit COMPUTER
module COMPUTER (
);

  wire BTN_INTR0_out, BTN_INTR1_out, BTN_INTR2_out, BTN_INTR3_out, BTN_INTR4_out, BTN_INTR5_out,
       BTN_INTR6_out, BTN_INTR7_out, BTN_RST_out, CLK, cpu_1_inta, pull_resistor_3_node,
       pull_resistor_6_node, ram_1_out_8, rst;
  wire [2:0] cpu_1_uext2__0;
  wire [7:0] interrupt_interface_8_1_intr7__0, pull_resistor_4_node, ram_1_out_7;
  wire [15:0] pull_resistor_2_node;

  Button BTN_RST (.out(BTN_RST_out));
  Clock u_CLK (.out(CLK));
  // RisingEdge risingedge_1: pin names not known; wires that end beside it: BTN_RST_out, CLK, rst
  // Probe on rst
  RAM ram_1 (
    .in_1(pull_resistor_2_node), .in_2(CLK), .in_3(pull_resistor_4_node), .in_4(pull_resistor_3_node),
    .in_5(pull_resistor_6_node), .in_6(rst), .out_7(ram_1_out_7), .out_8(ram_1_out_8));
  Pull_Resistor pull_resistor_1 (.node(ram_1_out_7));
  Pull_Resistor pull_resistor_2 (.node(pull_resistor_2_node));
  Pull_Resistor pull_resistor_3 (.node(pull_resistor_3_node));
  Pull_Resistor pull_resistor_4 (.node(pull_resistor_4_node));
  Pull_Resistor pull_resistor_5 (.node(ram_1_out_8));
  Pull_Resistor pull_resistor_6 (.node(pull_resistor_6_node));
  CPU cpu_1 (
    .in_1(rst), .in_2(CLK), .in_3(ram_1_out_8), .in_4(ram_1_out_7), .ABUS(pull_resistor_2_node),
    .DOUTBUS(pull_resistor_4_node), .out_8(pull_resistor_3_node), .out_9(pull_resistor_6_node),
    .inta(cpu_1_inta), .intr7__0(interrupt_interface_8_1_intr7__0), .UEXT2__0(cpu_1_uext2__0));
  INTERRUPT_INTERFACE_8 interrupt_interface_8_1 (
    .BTN_INTR0(BTN_INTR0_out), .BTN_INTR1(BTN_INTR1_out), .BTN_INTR2(BTN_INTR2_out),
    .BTN_INTR3(BTN_INTR3_out), .BTN_INTR4(BTN_INTR4_out), .BTN_INTR5(BTN_INTR5_out),
    .BTN_INTR6(BTN_INTR6_out), .BTN_INTR7(BTN_INTR7_out), .inta(cpu_1_inta), .UEXT2__0(cpu_1_uext2__0),
    .CLK(CLK), .intr7__0(interrupt_interface_8_1_intr7__0));
  Button BTN_INTR7 (.out(BTN_INTR7_out));
  Button BTN_INTR6 (.out(BTN_INTR6_out));
  Button BTN_INTR5 (.out(BTN_INTR5_out));
  Button BTN_INTR4 (.out(BTN_INTR4_out));
  Button BTN_INTR3 (.out(BTN_INTR3_out));
  Button BTN_INTR2 (.out(BTN_INTR2_out));
  Button BTN_INTR1 (.out(BTN_INTR1_out));
  Button BTN_INTR0 (.out(BTN_INTR0_out));
endmodule

module CPU (
  input  in_1,
  input  in_2,
  input  in_3,
  input  [7:0] in_4,
  input  [7:0] intr7__0,
  output [15:0] ABUS,
  output [7:0] DOUTBUS,
  output out_8,
  output out_9,
  output inta,
  output [2:0] UEXT2__0
);

  wire cout;
  wire [3:0] common_1_phaseffbus;
  wire [5:0] common_1_addrbus;
  wire [6:0] pull_resistor_1_node;
  wire [7:0] pull_resistor_4_node;
  wire [15:0] A, ALU, B, INTRADDR, PSW, pull_resistor_5_node, pull_resistor_6_node;
  wire [19:0] common_1_instrucbus;

  COMMON common_1 (
    .CLK(in_2), .RST(in_1), .DIN(in_4), .CMEMBUS(pull_resistor_6_node), .MAR(ABUS), .MDR(DOUTBUS),
    .PHASEFFBUS(common_1_phaseffbus), .INSTRUCBUS(common_1_instrucbus), .ADDRBUS(common_1_addrbus),
    .PSW(PSW), .CREGBUS(pull_resistor_5_node), .CFFBUS(pull_resistor_4_node), .B(B),
    .CPSW(pull_resistor_1_node), .ALU(ALU), .IVTPPDSP(INTRADDR), .in_6(cout), .A15__0(A));
  Pull_Resistor pull_resistor_1 (.node(pull_resistor_1_node));
  Pull_Resistor pull_resistor_2 (.node(common_1_phaseffbus));
  Pull_Resistor pull_resistor_3 (.node(common_1_instrucbus));
  Pull_Resistor pull_resistor_4 (.node(pull_resistor_4_node));
  Pull_Resistor pull_resistor_5 (.node(pull_resistor_5_node));
  Pull_Resistor pull_resistor_6 (.node(pull_resistor_6_node));
  Pull_Resistor pull_resistor_7 (.node(common_1_addrbus));
  FETCH fetch_1 (
    .in_1(in_1), .in_2(in_2), .in_3(in_3), .PHASEFFBUS(common_1_phaseffbus),
    .INSTRUCBUS(common_1_instrucbus), .ADDRBUS(common_1_addrbus), .PSW(PSW), .rdMEM(out_9),
    .CMEMBUS(pull_resistor_6_node), .CFFBUS(pull_resistor_4_node), .CREGBUS(pull_resistor_5_node));
  ADDR addr_1 (
    .in_1(in_1), .in_2(in_2), .in_3(in_3), .PHASEFFBUS(common_1_phaseffbus),
    .INSTRUCBUS(common_1_instrucbus), .ADDRBUS(common_1_addrbus), .CMEMBUS(pull_resistor_6_node),
    .CFFBUS(pull_resistor_4_node), .CREGBUS(pull_resistor_5_node), .out_10(out_9));
  EXEC exec_1 (
    .in_1(in_1), .in_2(in_2), .in_3(in_3), .B(B), .PHASEFFBUS(common_1_phaseffbus),
    .INSTRUCBUS(common_1_instrucbus), .ADDRBUS(common_1_addrbus), .PSW(PSW), .ALU(ALU),
    .CMEMBUS(pull_resistor_6_node), .CFFBUS(pull_resistor_4_node), .CREGBUS(pull_resistor_5_node),
    .CPSW(pull_resistor_1_node), .rdMEM(out_9), .wrMEM(out_8), .in_6(DOUTBUS), .in_7(ABUS), .out_13(cout),
    .A(A));
  INTR intr_1 (
    .ADDIVTP(INTRADDR), .UEXT2__0(UEXT2__0), .inta(inta), .in_1(in_1), .in_2(in_2),
    .CMEMBUS(pull_resistor_6_node), .in_3(in_3), .PHASEFFBUS(common_1_phaseffbus),
    .INSTRUCBUS(common_1_instrucbus), .CFFBUS(pull_resistor_4_node), .PSW(PSW), .intr(intr7__0),
    .CREGBUS(pull_resistor_5_node), .rdMEM(out_9), .wrMEM(out_8));

  // Other names for the same wires on the sheet: CLK = in_2; DIN7__0[7:0] = in_4; FCBUS = in_3; MAR[15:0] = ABUS;
  //   MDR[7:0] = DOUTBUS; RD = out_9; rst = in_1; WR = out_8
endmodule

module COMMON (
  input  CLK,
  input  RST,
  input  [7:0] DIN,
  input  [15:0] ALU,
  input  [15:0] IVTPPDSP,
  input  in_6,
  input  [15:0] CMEMBUS,
  input  [7:0] CFFBUS,
  input  [15:0] CREGBUS,
  input  [6:0] CPSW,
  output [15:0] A15__0,
  output [15:0] MAR,
  output [7:0] MDR,
  output [3:0] PHASEFFBUS,
  output [19:0] INSTRUCBUS,
  output [5:0] ADDRBUS,
  output [15:0] PSW,
  output [15:0] B
);

  wire ADRINST, adrinst_t, and_1_out, and_2_out, and_3_out, and_4_out, and_5_out, and_6_out, and_7_out,
       and_8_out, and_9_out, and_10_out, and_11_out, and_12_out, and_13_out, and_14_out, and_15_out,
       and_16_out, and_17_out, and_18_out, and_19_out, and_20_out, and_21_out, and_22_out, and_24_out,
       bezadrinst, branchinst, jmpinst, mp2_16b_1_p3, mp4_16b_1_p5, mp8_16b_1_p8, mp8_16b_2_p8,
       mp8_16b_2_p10, mp8_16b_3_p8, not_1_out, not_2_out, not_4_out, not_5_out, or_2_out, or_3_out, or_4_out,
       or_5_out, or_6_out, or_7_out, or_8_out, or_9_out, reg16_inc_ld_2_p4, rsff_2_p4, rsff_5_p4, rsff_6_p3,
       rsff_6_p4, rsff_7_p3, rsff_7_p4, rsff_8_p4, rsff_9_p4, rsff_10_p4;
  wire [3:0] IR27__24;
  wire [7:0] DWH, DWL, IR7__0, IR15__8, IR23__16, mp16_8b_1_y;
  wire [7:4] IR31__24;
  wire [15:0] ADDPCPOM15__0, ADDPCREL15__0, DEC_B, DEC_MAR, GPR15__0, mp2_16b_2_p3, PC15__0, SP15__0;

  // ADD16 add16_1: pin names not known; wires that end beside it: {{9{IR15__8[7]}}, IR15__8[6:0]}, ADDPCREL15__0, PC15__0, 1'b0
  // MP8_16b mp8_16b_1: pin names not known; wires that end beside it: CMEMBUS[7], CMEMBUS[6], CMEMBUS[5], PC15__0, {IR15__8, IR7__0}, B, GPR15__0, mp8_16b_1_p8, ADDPCREL15__0, SP15__0, DEC_MAR, IVTPPDSP, 1'b1
  // REG16_INC_LD reg16_inc_ld_1: pin names not known; wires that end beside it: CLK, mp8_16b_1_p8, MAR, CMEMBUS[0], CMEMBUS[8]
  // MP8_16b mp8_16b_2: pin names not known; wires that end beside it: CREGBUS[7], CREGBUS[6], CREGBUS[5], {IR15__8, IR7__0}, {MDR, {8{1'b0}}}, {B[15:8], MDR}, GPR15__0, mp8_16b_2_p8, DEC_B, mp8_16b_2_p10, mp8_16b_2_p10, 1'b1
  // REG16_LD reg16_ld_1: pin names not known; wires that end beside it: CLK, mp8_16b_2_p8, B, CREGBUS[4]
  // REG8_LD reg8_ld_1: pin names not known; wires that end beside it: CLK, MDR, {IR31__24, IR27__24}, CREGBUS[3]
  // REG8_LD reg8_ld_2: pin names not known; wires that end beside it: CLK, MDR, IR15__8, CREGBUS[1]
  // DC2_4 dc2_4_1: pin names not known; wires that end beside it: IR31__24[5:4], PSW[0], bezadrinst, branchinst, jmpinst, adrinst_t
  // DC3_8 dc3_8_1: pin names not known; wires that end beside it: IR27__24[2:0], bezadrinst, INSTRUCBUS[0], INSTRUCBUS[1], INSTRUCBUS[2], INSTRUCBUS[3], INSTRUCBUS[4], INSTRUCBUS[5]
  // DC3_8 dc3_8_2: pin names not known; wires that end beside it: IR27__24[2:0], branchinst, INSTRUCBUS[6], INSTRUCBUS[7], INSTRUCBUS[8], INSTRUCBUS[9], INSTRUCBUS[17]
  // ADD16 add16_2: pin names not known; wires that end beside it: {{9{IR23__16[7]}}, IR23__16[6:0]}, ADDPCPOM15__0, PC15__0, 1'b0
  // REG8_LD reg8_ld_3: pin names not known; wires that end beside it: CLK, MDR, IR23__16, CREGBUS[2]
  // REG8_LD reg8_ld_4: pin names not known; wires that end beside it: CLK, MDR, IR7__0, CREGBUS[0]
  // SUB16 sub16_1: pin names not known; wires that end beside it: MAR, DEC_MAR, 16'h1, 1'b0
  // SUB16 sub16_2: pin names not known; wires that end beside it: B, DEC_B, 16'h1, 1'b0
  MP16_8b mp16_8b_1 (
    .I0(DIN), .I1(A15__0[15:8]), .I2(A15__0[7:0]), .I3(PC15__0[15:8]), .I4(PC15__0[7:0]), .I5(B[7:0]),
    .I6(B[15:8]), .I7({PSW[15], {7{1'b0}}}), .S3(CMEMBUS[1]), .S2(CMEMBUS[11]), .S1(CMEMBUS[10]),
    .S0(CMEMBUS[9]), .I8({3'b000, PSW[4:0]}), .Y(mp16_8b_1_y));  // open: I9, I10, I11, I12, I13, I14, I15
  // REG8_LD reg8_ld_5: pin names not known; wires that end beside it: CLK, mp16_8b_1_y, MDR, CMEMBUS[2]
  // REG8_LD reg8_ld_6: pin names not known; wires that end beside it: CLK, MDR, DWH, CREGBUS[11]
  // DC1_2 dc1_2_1: pin names not known; wires that end beside it: IR27__24[0], jmpinst, INSTRUCBUS[18], INSTRUCBUS[19]
  // DC3_8 dc3_8_3: pin names not known; wires that end beside it: IR27__24[2:0], adrinst_t, INSTRUCBUS[10], INSTRUCBUS[11], INSTRUCBUS[12], INSTRUCBUS[13], INSTRUCBUS[14], INSTRUCBUS[15], INSTRUCBUS[16]
  // DC3_8 dc3_8_4: pin names not known; wires that end beside it: IR23__16[6:4], adrinst_t, ADDRBUS[0], ADDRBUS[1], ADDRBUS[2], ADDRBUS[3], ADDRBUS[4], ADDRBUS[5]
  // MP4_16b mp4_16b_1: pin names not known; wires that end beside it: CMEMBUS[15], CMEMBUS[14], {DWH, DWL}, ADDPCPOM15__0, mp4_16b_1_p5, {IR23__16, IR15__8}, 1'b1
  // REG16 reg16_1: pin names not known; wires that end beside it: CLK, 16'hf000, SP15__0, RST, CMEMBUS[12], CMEMBUS[13]
  // MP8_16b mp8_16b_3: pin names not known; wires that end beside it: CREGBUS[15], CREGBUS[14], CREGBUS[13], B, ALU, {A15__0[0], A15__0[15:1]}, {{8{1'b0}}, MDR}, mp8_16b_3_p8, {MDR, A15__0[7:0]}, MAR, {16{1'b1}}, 1'b1
  not not_1 (not_1_out, RST);
  // REG16_LD reg16_ld_2: pin names not known; wires that end beside it: CLK, not_1_out, mp8_16b_3_p8, A15__0, CREGBUS[12]
  // MP2_16b mp2_16b_1: pin names not known; wires that end beside it: RST, mp4_16b_1_p5, mp2_16b_1_p3, 16'h1000, 1'b1
  // REG16_INC_LD reg16_inc_ld_2: pin names not known; wires that end beside it: CLK, mp2_16b_1_p3, PC15__0, reg16_inc_ld_2_p4, CMEMBUS[4]
  // REG8_LD reg8_ld_7: pin names not known; wires that end beside it: CLK, MDR, DWL, CREGBUS[10]
  or or_1 (reg16_inc_ld_2_p4, CMEMBUS[3], RST);
  or or_2 (or_2_out, ADRINST, INSTRUCBUS[3], INSTRUCBUS[5]);
  and and_1 (and_1_out, ~ALU[15], ~B[15], A15__0[15]);  // AND_Gate
  or or_3 (or_3_out, and_1_out, and_2_out);
  and and_2 (and_2_out, ALU[15], B[15], ~A15__0[15]);  // AND_Gate
  not not_2 (not_2_out, RST);
  // RSFF rsff_1: pin names not known; wires that end beside it: CFFBUS[1], CLK, CFFBUS[0], not_2_out, PHASEFFBUS[0]
  or or_4 (or_4_out, ADRINST, INSTRUCBUS[3], INSTRUCBUS[5]);
  and and_3 (and_3_out, ~A15__0[0], ~A15__0[1], ~A15__0[2], ~A15__0[3], ~A15__0[4], ~A15__0[5], ~A15__0[6], ~A15__0[7], ~A15__0[8], ~A15__0[9], ~A15__0[10], ~A15__0[11], ~A15__0[12], ~A15__0[13], ~A15__0[14], ~A15__0[15]);  // AND_Gate
  and and_4 (and_4_out, MDR[2], INSTRUCBUS[2]);
  and and_5 (and_5_out, or_2_out, A15__0[15]);
  and and_6 (and_6_out, MDR[3], INSTRUCBUS[2]);
  and and_7 (and_7_out, INSTRUCBUS[13], or_3_out);
  and and_8 (and_8_out, MDR[4], INSTRUCBUS[2]);
  and and_9 (and_9_out, INSTRUCBUS[13], in_6);
  and and_10 (and_10_out, INSTRUCBUS[3], A15__0[15]);
  and and_11 (and_11_out, MDR[7], INSTRUCBUS[2]);
  // RSFF rsff_2: pin names not known; wires that end beside it: CFFBUS[5], CLK, CFFBUS[4], rsff_2_p4, PHASEFFBUS[2]
  not not_3 (rsff_2_p4, RST);
  and and_12 (and_12_out, MDR[1], INSTRUCBUS[2]);
  or or_5 (or_5_out, and_12_out, and_13_out);
  and and_13 (and_13_out, or_4_out, and_3_out);
  or or_6 (or_6_out, and_4_out, and_5_out);
  or or_7 (or_7_out, and_6_out, and_7_out);
  or or_8 (or_8_out, and_8_out, and_9_out, and_10_out);
  and and_14 (and_14_out, ~and_11_out, CPSW[1]);  // AND_Gate
  and and_15 (and_15_out, and_11_out, CPSW[1]);
  // MP2_16b mp2_16b_2: pin names not known; wires that end beside it: CREGBUS[9], A15__0, mp2_16b_2_p3, B, 1'b1
  GPR16x16 gpr16x16_1 (.DI15__0(mp2_16b_2_p3), .A3__0(IR23__16[3:0]), .WR(CREGBUS[8]), .CLK(CLK), .DO15__0(GPR15__0));
  and and_16 (and_16_out, ~MDR[0], INSTRUCBUS[2], CPSW[6]);  // AND_Gate
  or or_9 (or_9_out, and_16_out, CPSW[0]);
  and and_17 (and_17_out, MDR[0], INSTRUCBUS[2], CPSW[6]);
  and and_18 (and_18_out, ~or_6_out, CPSW[4]);  // AND_Gate
  and and_19 (and_19_out, or_6_out, CPSW[4]);
  not not_4 (not_4_out, RST);
  // RSFF rsff_3: pin names not known; wires that end beside it: and_14_out, CLK, and_15_out, not_4_out, PSW[15]
  or or_10 (ADRINST, INSTRUCBUS[10], INSTRUCBUS[12], INSTRUCBUS[13], INSTRUCBUS[14], INSTRUCBUS[15], INSTRUCBUS[16]);
  not not_5 (not_5_out, RST);
  // RSFF rsff_4: pin names not known; wires that end beside it: or_9_out, CLK, and_17_out, not_5_out, PSW[0]
  and and_20 (and_20_out, ~or_5_out, CPSW[5]);  // AND_Gate
  and and_21 (and_21_out, or_5_out, CPSW[5]);
  // RSFF rsff_5: pin names not known; wires that end beside it: and_18_out, CLK, and_19_out, rsff_5_p4, PSW[2]
  not not_6 (rsff_5_p4, RST);
  and and_22 (and_22_out, ~or_7_out, CPSW[2]);  // AND_Gate
  // RSFF rsff_6: pin names not known; wires that end beside it: and_22_out, CLK, rsff_6_p3, rsff_6_p4, PSW[3]
  not not_7 (rsff_6_p4, RST);
  and and_23 (rsff_6_p3, or_7_out, CPSW[2]);
  and and_24 (and_24_out, ~or_8_out, CPSW[3]);  // AND_Gate
  // RSFF rsff_7: pin names not known; wires that end beside it: and_24_out, CLK, rsff_7_p3, rsff_7_p4, PSW[4]
  not not_8 (rsff_7_p4, RST);
  and and_25 (rsff_7_p3, or_8_out, CPSW[3]);
  // RSFF rsff_8: pin names not known; wires that end beside it: CFFBUS[3], CLK, CFFBUS[2], rsff_8_p4, PHASEFFBUS[1]
  not not_9 (rsff_8_p4, RST);
  // RSFF rsff_9: pin names not known; wires that end beside it: CFFBUS[7], CLK, CFFBUS[6], rsff_9_p4, PHASEFFBUS[3]
  not not_10 (rsff_9_p4, RST);
  // RSFF rsff_10: pin names not known; wires that end beside it: and_20_out, CLK, and_21_out, rsff_10_p4, PSW[1]
  not not_11 (rsff_10_p4, RST);

  assign PSW[14:5] = {10{1'b0}};

  // Other names for the same wires on the sheet: A0 = A15__0[0]; A7__0[7:0] = A15__0[7:0];
  //   A15__1[14:0] = A15__0[15:1]; MDR7__0[7:0] = MDR; A15 = A15__0[15]; ADDIVTP15__0[15:0] = IVTPPDSP;
  //   immed = ADDRBUS[0]; memind = ADDRBUS[1]; regdir = ADDRBUS[2]; regind = ADDRBUS[3]; predec = ADDRBUS[4];
  //   pcrelpom = ADDRBUS[5]; ALU15__0[15:0] = ALU; B15__0[15:0] = B; B15__8[7:0] = B[15:8]; stFETCH = CFFBUS[0];
  //   clFETCH = CFFBUS[1]; stADDR = CFFBUS[2]; clADDR = CFFBUS[3]; stEXEC = CFFBUS[4]; clEXEC = CFFBUS[5];
  //   stINTR = CFFBUS[6]; clINTR = CFFBUS[7]; ldMAR = CMEMBUS[0]; mxMDR3 = CMEMBUS[1]; ldMDR = CMEMBUS[2];
  //   ldPC = CMEMBUS[3]; incPC = CMEMBUS[4]; mxMAR0 = CMEMBUS[5]; mxMAR1 = CMEMBUS[6]; mxMAR2 = CMEMBUS[7];
  //   incMAR = CMEMBUS[8]; mxMDR0 = CMEMBUS[9]; mxMDR1 = CMEMBUS[10]; mxMDR2 = CMEMBUS[11]; incSP = CMEMBUS[12];
  //   decSP = CMEMBUS[13]; mxPC0 = CMEMBUS[14]; mxPC1 = CMEMBUS[15]; cout = in_6; clPSWSTART = CPSW[0]; ldI = CPSW[1];
  //   ldV = CPSW[2]; ldC = CPSW[3]; ldN = CPSW[4]; ldZ = CPSW[5]; ldSTART = CPSW[6]; ldIR7__0 = CREGBUS[0];
  //   ldIR15__8 = CREGBUS[1]; ldIR23__16 = CREGBUS[2]; ldIR31__24 = CREGBUS[3]; ldB = CREGBUS[4]; mxB0 = CREGBUS[5];
  //   mxB1 = CREGBUS[6]; mxB2 = CREGBUS[7]; wrGPR = CREGBUS[8]; mxGPR0 = CREGBUS[9]; ldDWL = CREGBUS[10];
  //   ldDWH = CREGBUS[11]; ldA = CREGBUS[12]; mxA0 = CREGBUS[13]; mxA1 = CREGBUS[14]; mxA2 = CREGBUS[15];
  //   Din7__0[7:0] = DIN; HALT = INSTRUCBUS[0]; RTS = INSTRUCBUS[1]; RTI = INSTRUCBUS[2]; ROR = INSTRUCBUS[3];
  //   PUSH = INSTRUCBUS[4]; POP = INSTRUCBUS[5]; BOVF = INSTRUCBUS[6]; BNCR = INSTRUCBUS[7]; BLEQ = INSTRUCBUS[8];
  //   BLSSU = INSTRUCBUS[9]; LD = INSTRUCBUS[10]; ST = INSTRUCBUS[11]; DEC = INSTRUCBUS[12]; SUB = INSTRUCBUS[13];
  //   XOR = INSTRUCBUS[14]; AND = INSTRUCBUS[15]; STRFIND = INSTRUCBUS[16]; JLEQ = INSTRUCBUS[17];
  //   JMP = INSTRUCBUS[18]; JSR = INSTRUCBUS[19]; IR31__24[3:0] = IR27__24; MAR15__0[15:0] = MAR;
  //   FETCH = PHASEFFBUS[0]; ADDR = PHASEFFBUS[1]; EXEC = PHASEFFBUS[2]; INTR = PHASEFFBUS[3];
  //   PSW15__0 (some bits) = {PSW[15], PSW[4:0]}; PSWSTART = PSW[0]; PSWZ = PSW[1]; PSWN = PSW[2]; PSWV = PSW[3];
  //   PSWC = PSW[4]; PSWI = PSW[15]

  // Notes on the sheet:
  //   Instrukcijski registar
  //   Pomocni registri
  //   Sabiraci i oduzimaci
  //   MAR
  //   MDR
  //   Dekoderi za prepoznavanje instrukcije na osnovu sadrzaja registra IR31..24
  //   Dekoderi za prepoznavanje nacina adresiranja
  //   PC
  //   SP
  //   Akumulator
  //   Registarski fajl
  //   FF za pokretanje FETCH, ADDR, EXEC i INTR faze izvršavanja instrukcije
  //   Programska statusna reč (PSW)
endmodule

module FETCH (
  input  in_1,
  input  in_2,
  input  in_3,
  input  [3:0] PHASEFFBUS,
  input  [19:0] INSTRUCBUS,
  input  [5:0] ADDRBUS,
  input  [15:0] PSW,
  output [15:0] CMEMBUS,
  output [7:0] CFFBUS,
  output [15:0] CREGBUS,
  output rdMEM
);

  wire addr2, addr3, addr_t, and_3_out, and_4_out, and_5_out, and_6_out, and_7_out, and_8_out, and_9_out,
       and_10_out, and_11_out, and_12_out, and_13_out, and_14_out, bezadr1, bradr2, bradr3, brbezadr1, brcnd,
       brgradr, brgrinst, brjmp2, brjmp3, brnotfcmem, bruncnd, clFETCH, gradr, grinst, incPC, jmp2, jmp3,
       ldIR7__0, ldIR15__8, ldIR23__16, ldIR31__24, ldMAR, ldMDR, nor_2_out, not_1_out, not_3_out, not_4_out,
       not_5_out, notPSWSTandFETCH, or_5_out, or_7_out, rdMEM_t, reg5_cl_inc_ld_1_p6, reg5_cl_inc_ld_1_p7,
       stADDR, stEXEC;
  wire [3:0] rom32x24_fetch_1_dout_2;
  wire [4:0] reg5_cl_inc_ld_1_p4, reg5_cl_inc_ld_1_p5;
  wire [23:11] rom32x24_fetch_1_dout;

  or or_1 (bezadr1, INSTRUCBUS[0], INSTRUCBUS[1], INSTRUCBUS[2], INSTRUCBUS[3], INSTRUCBUS[4], INSTRUCBUS[5]);
  or or_2 (jmp2, INSTRUCBUS[6], INSTRUCBUS[7], INSTRUCBUS[8], INSTRUCBUS[9]);
  or or_3 (jmp3, INSTRUCBUS[17], INSTRUCBUS[18], INSTRUCBUS[19]);
  not not_1 (not_1_out, in_1);
  // REG5_CL_INC_LD reg5_cl_inc_ld_1: pin names not known; wires that end beside it: 1'b0, in_2, not_1_out, reg5_cl_inc_ld_1_p4, reg5_cl_inc_ld_1_p5, reg5_cl_inc_ld_1_p6, reg5_cl_inc_ld_1_p7
  not not_2 (reg5_cl_inc_ld_1_p7, reg5_cl_inc_ld_1_p6);
  or or_4 (reg5_cl_inc_ld_1_p6, bruncnd, brcnd);
  ROM32x24_FETCH rom32x24_fetch_1 (
    .A4__0(reg5_cl_inc_ld_1_p5), .CS(1'b1),
    .DOUT({rom32x24_fetch_1_dout[23:21], reg5_cl_inc_ld_1_p4, rom32x24_fetch_1_dout_2, rom32x24_fetch_1_dout[11], stEXEC, stADDR, clFETCH, ldIR7__0, ldIR15__8, ldIR23__16, ldIR31__24, ldMDR, rdMEM_t, incPC, ldMAR}));
  // DC4_16 dc4_16_1: pin names not known; wires that end beside it: rom32x24_fetch_1_dout_2, 1'b1, bruncnd, notPSWSTandFETCH, brbezadr1, brjmp2, bradr2, brjmp3, bradr3, brnotfcmem, brgrinst, brgradr
  and and_1 (addr2, addr_t, or_5_out);
  or or_5 (or_5_out, ADDRBUS[2], ADDRBUS[3], ADDRBUS[4]);
  and and_2 (addr3, addr_t, ADDRBUS[5]);
  or or_6 (addr_t, INSTRUCBUS[10], INSTRUCBUS[11], INSTRUCBUS[12], INSTRUCBUS[13], INSTRUCBUS[14], INSTRUCBUS[15], INSTRUCBUS[16]);
  not not_3 (not_3_out, PHASEFFBUS[0]);
  not not_4 (not_4_out, PSW[0]);
  or or_7 (or_7_out, not_3_out, not_4_out);
  not not_5 (not_5_out, in_3);
  nor nor_1 (grinst, INSTRUCBUS[0], INSTRUCBUS[1], INSTRUCBUS[2], INSTRUCBUS[3], INSTRUCBUS[4], INSTRUCBUS[5], INSTRUCBUS[6], INSTRUCBUS[7], INSTRUCBUS[8], INSTRUCBUS[9], INSTRUCBUS[10], INSTRUCBUS[11], INSTRUCBUS[12], INSTRUCBUS[13], INSTRUCBUS[14], INSTRUCBUS[15], INSTRUCBUS[16], INSTRUCBUS[17], INSTRUCBUS[18], INSTRUCBUS[19]);
  and and_3 (and_3_out, or_7_out, notPSWSTandFETCH);
  and and_4 (and_4_out, brbezadr1, bezadr1);
  and and_5 (and_5_out, brjmp2, jmp2);
  and and_6 (and_6_out, bradr2, addr2);
  and and_7 (and_7_out, brjmp3, jmp3);
  and and_8 (and_8_out, bradr3, addr3);
  and and_9 (and_9_out, brnotfcmem, not_5_out);
  and and_10 (and_10_out, brgrinst, grinst);
  and and_11 (and_11_out, brgradr, gradr);
  and and_12 (and_12_out, INSTRUCBUS[11], ADDRBUS[0]);
  nor nor_2 (nor_2_out, ADDRBUS[0], ADDRBUS[1], ADDRBUS[2], ADDRBUS[3], ADDRBUS[4], ADDRBUS[5]);
  and and_13 (and_13_out, INSTRUCBUS[12], ADDRBUS[0]);
  or or_8 (brcnd, and_3_out, and_4_out, and_5_out, and_6_out, and_7_out, and_8_out, and_9_out, and_10_out, and_11_out);
  and and_14 (and_14_out, nor_2_out, addr_t);
  or or_9 (gradr, and_12_out, and_14_out, and_13_out);
  assign CMEMBUS[0] = ldMAR ? 1'b1 : 1'bz;  // Controlled_Buffer controlled_buffer_1
  assign CMEMBUS[2] = ldMDR ? 1'b1 : 1'bz;  // Controlled_Buffer controlled_buffer_2
  assign CMEMBUS[4] = incPC ? 1'b1 : 1'bz;  // Controlled_Buffer controlled_buffer_3
  assign CFFBUS[1] = clFETCH ? 1'b1 : 1'bz;  // Controlled_Buffer controlled_buffer_4
  assign CFFBUS[2] = stADDR ? 1'b1 : 1'bz;  // Controlled_Buffer controlled_buffer_5
  assign CFFBUS[4] = stEXEC ? 1'b1 : 1'bz;  // Controlled_Buffer controlled_buffer_6
  assign CREGBUS[0] = ldIR7__0 ? 1'b1 : 1'bz;  // Controlled_Buffer controlled_buffer_7
  assign CREGBUS[1] = ldIR15__8 ? 1'b1 : 1'bz;  // Controlled_Buffer controlled_buffer_8
  assign CREGBUS[2] = ldIR23__16 ? 1'b1 : 1'bz;  // Controlled_Buffer controlled_buffer_9
  assign CREGBUS[3] = ldIR31__24 ? 1'b1 : 1'bz;  // Controlled_Buffer controlled_buffer_10
  assign rdMEM = rdMEM_t ? 1'b1 : 1'bz;  // Controlled_Buffer controlled_buffer_11

  // Other names for the same wires on the sheet: immed = ADDRBUS[0]; memind = ADDRBUS[1]; regdir = ADDRBUS[2];
  //   regind = ADDRBUS[3]; predec = ADDRBUS[4]; pcrelpom = ADDRBUS[5]; CLK = in_2; FCBUS = in_3; HALT = INSTRUCBUS[0];
  //   RTS = INSTRUCBUS[1]; RTI = INSTRUCBUS[2]; ROR = INSTRUCBUS[3]; PUSH = INSTRUCBUS[4]; POP = INSTRUCBUS[5];
  //   BOVF = INSTRUCBUS[6]; BNCR = INSTRUCBUS[7]; BLEQ = INSTRUCBUS[8]; BLSSU = INSTRUCBUS[9]; LD = INSTRUCBUS[10];
  //   ST = INSTRUCBUS[11]; DEC = INSTRUCBUS[12]; SUB = INSTRUCBUS[13]; XOR = INSTRUCBUS[14]; AND = INSTRUCBUS[15];
  //   STRFIND = INSTRUCBUS[16]; JLEQ = INSTRUCBUS[17]; JMP = INSTRUCBUS[18]; JSR = INSTRUCBUS[19];
  //   FETCH = PHASEFFBUS[0]; ADDR = PHASEFFBUS[1]; EXEC = PHASEFFBUS[2]; INTR = PHASEFFBUS[3]; PSWSTART = PSW[0];
  //   rst = in_1

  // Notes on the sheet:
  //   Operaciona jedinica
  //   Kontrolna jedinica
endmodule

module ADDR (
  input  in_1,
  input  in_2,
  input  in_3,
  input  [3:0] PHASEFFBUS,
  input  [19:0] INSTRUCBUS,
  input  [5:0] ADDRBUS,
  output [15:0] CMEMBUS,
  output [7:0] CFFBUS,
  output [15:0] CREGBUS,
  output out_10
);

  wire and_1_out, and_2_out, and_3_out, bradr, brcnd, brnotADDR, brnotfcbus, brSTORE, bruncnd, clADDR,
       incMAR, ldB, ldMAR, ldMDR, mxB0, mxB1, mxB2, mxGPR0, mxMAR0, mxMAR1, mxMAR2, not_1_out, not_3_out,
       not_4_out, rdMEM, reg5_cl_inc_ld_1_p6, reg5_cl_inc_ld_1_p7, stEXEC, wrGPR;
  wire [2:0] rom32x24_addr_1_dout;
  wire [4:0] kmadr_1_adr4__0, mp2_5b_1_y, reg5_cl_inc_ld_1_p5, rom32x24_addr_1_dout_3;
  wire [15:15] rom32x24_addr_1_dout_2;

  not not_1 (not_1_out, in_1);
  MP2_5b mp2_5b_1 (.En(1'b1), .in_2(rom32x24_addr_1_dout_3), .in_3(kmadr_1_adr4__0), .S0(bradr), .Y(mp2_5b_1_y));
  // REG5_CL_INC_LD reg5_cl_inc_ld_1: pin names not known; wires that end beside it: 1'b0, in_2, not_1_out, mp2_5b_1_y, reg5_cl_inc_ld_1_p5, reg5_cl_inc_ld_1_p6, reg5_cl_inc_ld_1_p7
  not not_2 (reg5_cl_inc_ld_1_p7, reg5_cl_inc_ld_1_p6);
  ROM32x24_ADDR rom32x24_addr_1 (
    .A4__0(reg5_cl_inc_ld_1_p5), .CS(1'b1),
    .DOUT({rom32x24_addr_1_dout_3, rom32x24_addr_1_dout, rom32x24_addr_1_dout_2[15], stEXEC, clADDR, mxMAR2, mxGPR0, wrGPR, mxB2, mxB1, mxMAR1, incMAR, mxB0, ldB, rdMEM, ldMDR, mxMAR0, ldMAR}));
  // DC3_8 dc3_8_1: pin names not known; wires that end beside it: rom32x24_addr_1_dout, 1'b1, bruncnd, brnotADDR, brnotfcbus, brSTORE, bradr
  KMADR kmadr_1 (
    .immed(ADDRBUS[0]), .memind(ADDRBUS[1]), .regdir(ADDRBUS[2]), .regind(ADDRBUS[3]),
    .Adr4__0(kmadr_1_adr4__0), .pcrelpom(ADDRBUS[5]), .predec(ADDRBUS[4]));
  or or_1 (reg5_cl_inc_ld_1_p6, bruncnd, brcnd, bradr);
  not not_3 (not_3_out, PHASEFFBUS[1]);
  not not_4 (not_4_out, in_3);
  and and_1 (and_1_out, not_3_out, brnotADDR);
  and and_2 (and_2_out, INSTRUCBUS[11], brSTORE);
  and and_3 (and_3_out, brnotfcbus, not_4_out);
  or or_2 (brcnd, and_1_out, and_2_out, and_3_out);
  assign CMEMBUS[0] = ldMAR ? 1'b1 : 1'bz;  // Controlled_Buffer controlled_buffer_1
  assign CMEMBUS[2] = ldMDR ? 1'b1 : 1'bz;  // Controlled_Buffer controlled_buffer_2
  assign CMEMBUS[5] = mxMAR0 ? 1'b1 : 1'bz;  // Controlled_Buffer controlled_buffer_3
  assign CMEMBUS[6] = mxMAR1 ? 1'b1 : 1'bz;  // Controlled_Buffer controlled_buffer_4
  assign CMEMBUS[7] = mxMAR2 ? 1'b1 : 1'bz;  // Controlled_Buffer controlled_buffer_5
  assign CMEMBUS[8] = incMAR ? 1'b1 : 1'bz;  // Controlled_Buffer controlled_buffer_6
  assign CFFBUS[3] = clADDR ? 1'b1 : 1'bz;  // Controlled_Buffer controlled_buffer_7
  assign CFFBUS[4] = stEXEC ? 1'b1 : 1'bz;  // Controlled_Buffer controlled_buffer_8
  assign CREGBUS[4] = ldB ? 1'b1 : 1'bz;  // Controlled_Buffer controlled_buffer_9
  assign CREGBUS[5] = mxB0 ? 1'b1 : 1'bz;  // Controlled_Buffer controlled_buffer_10
  assign CREGBUS[6] = mxB1 ? 1'b1 : 1'bz;  // Controlled_Buffer controlled_buffer_11
  assign CREGBUS[7] = mxB2 ? 1'b1 : 1'bz;  // Controlled_Buffer controlled_buffer_12
  assign CREGBUS[8] = wrGPR ? 1'b1 : 1'bz;  // Controlled_Buffer controlled_buffer_13
  assign CREGBUS[9] = mxGPR0 ? 1'b1 : 1'bz;  // Controlled_Buffer controlled_buffer_14
  assign out_10 = rdMEM ? 1'b1 : 1'bz;  // Controlled_Buffer controlled_buffer_15

  // Other names for the same wires on the sheet: immed = ADDRBUS[0]; memind = ADDRBUS[1]; regdir = ADDRBUS[2];
  //   regind = ADDRBUS[3]; predec = ADDRBUS[4]; pcrelpom = ADDRBUS[5]; CLK = in_2; FCBUS = in_3; ST = INSTRUCBUS[11];
  //   ADDR = PHASEFFBUS[1]; rst = in_1

  // Notes on the sheet:
  //   Operaciona jedinica
  //   Upravljacka jedinica
endmodule

module EXEC (
  input  in_1,
  input  in_2,
  input  in_3,
  input  [15:0] A,
  input  [15:0] B,
  input  [7:0] in_6,
  input  [15:0] in_7,
  input  [3:0] PHASEFFBUS,
  input  [19:0] INSTRUCBUS,
  input  [5:0] ADDRBUS,
  input  [15:0] PSW,
  output [15:0] ALU,
  output out_13,
  output [15:0] CMEMBUS,
  output [7:0] CFFBUS,
  output [15:0] CREGBUS,
  output [6:0] CPSW,
  output rdMEM,
  output wrMEM
);

  wire and_1_out, and_2_out, and_3_out, and_4_out, and_5_out, and_6_out, and_7_out, and_8_out, and_9_out,
       and_10_out, and_t, brcnd, brnotbrorjmp, brnotequal, brnotEXEC, brnotFCBUS, bropr, brorjmp, brregdir,
       bruncnd, brzero, clEXEC, clPSWSTART, decSP, equal, incMAR, incSP, ldA, ldB, ldC, ldDWH, ldDWL, ldI,
       ldMAR, ldMDR, ldN, ldPC, ldSTART, ldV, ldZ, mxA0, mxA1, mxA2, mxB2, mxGPR0, mxMAR0, mxMAR1, mxMAR2,
       mxMDR0, mxMDR1, mxMDR2, mxPC0, mxPC1, not_1_out, not_2_out, not_3_out, not_4_out, not_5_out,
       not_6_out, or_1_out, or_2_out, or_3_out, rdMEM_t, stINTR, sub_t, wrGPR, wrMEM_t, xor_1_out, xor_t,
       zero;
  wire [6:0] kmopr_1_adr6__0, mp2_7b_1_y, reg7_inc_ld_1_a6__0;
  wire [19:6] rom128x52_1_dout51__32;

  ALU16_SUB_XOR_AND alu16_sub_xor_and_1 (
    .Cin(1'b0), .A(A), .B(B), .sub(sub_t), .\xor (xor_t), .\and (and_t), .F(ALU), .Cout(out_13));
  // DC4_16 dc4_16_1: pin names not known; wires that end beside it: rom128x52_1_dout51__32[11:8], 1'b1, bruncnd, brnotEXEC, brnotbrorjmp, brregdir, brzero, brnotequal, brnotFCBUS, bropr
  not not_1 (not_1_out, in_1);
  MP2_7b mp2_7b_1 (
    .En(1'b1), ._6__0(rom128x52_1_dout51__32[18:12]), .in_3(kmopr_1_adr6__0), .S0(bropr), .Y(mp2_7b_1_y));
  REG7_INC_LD reg7_inc_ld_1 (
    .I6__0(mp2_7b_1_y), .LD(or_1_out), .INC(not_2_out), .mr(not_1_out), .CLK(in_2),
    .A6__0(reg7_inc_ld_1_a6__0));
  KMOPR kmopr_1 (
    .HALT(INSTRUCBUS[0]), .RTS(INSTRUCBUS[1]), .RTI(INSTRUCBUS[2]), .ROR(INSTRUCBUS[3]),
    .PUSH(INSTRUCBUS[4]), .Adr6__0(kmopr_1_adr6__0), .POP(INSTRUCBUS[5]), .BOVF(INSTRUCBUS[6]),
    .BNCR(INSTRUCBUS[7]), .BLEQ(INSTRUCBUS[8]), .BLSSU(INSTRUCBUS[9]), .JLEQ(INSTRUCBUS[17]),
    .JMP(INSTRUCBUS[18]), .JSR(INSTRUCBUS[19]), .LD(INSTRUCBUS[10]), .ST(INSTRUCBUS[11]),
    .DEC(INSTRUCBUS[12]), .SUB(INSTRUCBUS[13]), .XOR(INSTRUCBUS[14]), .AND(INSTRUCBUS[15]),
    .STRFIND(INSTRUCBUS[16]));
  or or_1 (or_1_out, bruncnd, brcnd, bropr);
  not not_2 (not_2_out, or_1_out);
  ROM128x52 rom128x52_1 (
    .A5__0(reg7_inc_ld_1_a6__0), .CS(1'b1),
    .DOUT51__32({rom128x52_1_dout51__32, clEXEC, stINTR, and_t, xor_t, sub_t, ldB}),
    .DOUT31__0({mxB2, wrGPR, mxGPR0, ldA, mxA2, mxA1, mxA0, wrMEM_t, ldI, ldC, ldV, ldN, ldZ, ldSTART, ldPC, mxPC1, mxPC0, ldDWH, ldDWL, ldMDR, mxMDR2, mxMDR1, mxMDR0, rdMEM_t, incSP, decSP, incMAR, ldMAR, mxMAR2, mxMAR1, mxMAR0, clPSWSTART}));
  Comparator comparator_1 (.a(A[7:0]), .b(in_6), .eq(equal));  // open: gt, lt
  Comparator comparator_2 (.a({8{1'b0}}), .b(in_6), .eq(zero));  // open: gt, lt
  and and_1 (and_1_out, INSTRUCBUS[6], PSW[3]);
  xor xor_1 (xor_1_out, PSW[2], PSW[3]);
  and and_2 (and_2_out, INSTRUCBUS[7], ~PSW[4]);  // AND_Gate
  and and_3 (and_3_out, INSTRUCBUS[9], PSW[4]);
  or or_2 (or_2_out, xor_1_out, PSW[1]);
  or or_3 (or_3_out, INSTRUCBUS[8], INSTRUCBUS[17]);
  not not_3 (not_3_out, PHASEFFBUS[2]);
  not not_4 (not_4_out, brorjmp);
  not not_5 (not_5_out, equal);
  not not_6 (not_6_out, in_3);
  and and_4 (and_4_out, or_2_out, or_3_out);
  and and_5 (and_5_out, not_3_out, brnotEXEC);
  and and_6 (and_6_out, not_4_out, brnotbrorjmp);
  and and_7 (and_7_out, ADDRBUS[2], brregdir);
  and and_8 (and_8_out, zero, brzero);
  and and_9 (and_9_out, not_5_out, brnotequal);
  and and_10 (and_10_out, not_6_out, brnotFCBUS);
  or or_4 (brorjmp, and_1_out, and_4_out, and_2_out, and_3_out);
  or or_5 (brcnd, and_5_out, and_6_out, and_7_out, and_8_out, and_9_out, and_10_out);
  assign CMEMBUS[0] = ldMAR ? 1'b1 : 1'bz;  // Controlled_Buffer controlled_buffer_1
  assign CMEMBUS[2] = ldMDR ? 1'b1 : 1'bz;  // Controlled_Buffer controlled_buffer_2
  assign CMEMBUS[3] = ldPC ? 1'b1 : 1'bz;  // Controlled_Buffer controlled_buffer_3
  assign CMEMBUS[5] = mxMAR0 ? 1'b1 : 1'bz;  // Controlled_Buffer controlled_buffer_4
  assign CMEMBUS[6] = mxMAR1 ? 1'b1 : 1'bz;  // Controlled_Buffer controlled_buffer_5
  assign CMEMBUS[7] = mxMAR2 ? 1'b1 : 1'bz;  // Controlled_Buffer controlled_buffer_6
  assign CMEMBUS[8] = incMAR ? 1'b1 : 1'bz;  // Controlled_Buffer controlled_buffer_7
  assign CMEMBUS[9] = mxMDR0 ? 1'b1 : 1'bz;  // Controlled_Buffer controlled_buffer_8
  assign CMEMBUS[10] = mxMDR1 ? 1'b1 : 1'bz;  // Controlled_Buffer controlled_buffer_9
  assign CMEMBUS[11] = mxMDR2 ? 1'b1 : 1'bz;  // Controlled_Buffer controlled_buffer_10
  assign CMEMBUS[12] = incSP ? 1'b1 : 1'bz;  // Controlled_Buffer controlled_buffer_11
  assign CMEMBUS[13] = decSP ? 1'b1 : 1'bz;  // Controlled_Buffer controlled_buffer_12
  assign CMEMBUS[14] = mxPC0 ? 1'b1 : 1'bz;  // Controlled_Buffer controlled_buffer_13
  assign CMEMBUS[15] = mxPC1 ? 1'b1 : 1'bz;  // Controlled_Buffer controlled_buffer_14
  assign CFFBUS[5] = clEXEC ? 1'b1 : 1'bz;  // Controlled_Buffer controlled_buffer_15
  assign CFFBUS[6] = stINTR ? 1'b1 : 1'bz;  // Controlled_Buffer controlled_buffer_16
  assign CREGBUS[4] = ldB ? 1'b1 : 1'bz;  // Controlled_Buffer controlled_buffer_17
  assign CREGBUS[7] = mxB2 ? 1'b1 : 1'bz;  // Controlled_Buffer controlled_buffer_18
  assign CREGBUS[8] = wrGPR ? 1'b1 : 1'bz;  // Controlled_Buffer controlled_buffer_19
  assign CREGBUS[9] = mxGPR0 ? 1'b1 : 1'bz;  // Controlled_Buffer controlled_buffer_20
  assign CREGBUS[10] = ldDWL ? 1'b1 : 1'bz;  // Controlled_Buffer controlled_buffer_21
  assign CREGBUS[11] = ldDWH ? 1'b1 : 1'bz;  // Controlled_Buffer controlled_buffer_22
  assign CREGBUS[12] = ldA ? 1'b1 : 1'bz;  // Controlled_Buffer controlled_buffer_23
  assign CREGBUS[13] = mxA0 ? 1'b1 : 1'bz;  // Controlled_Buffer controlled_buffer_24
  assign CREGBUS[14] = mxA1 ? 1'b1 : 1'bz;  // Controlled_Buffer controlled_buffer_25
  assign CREGBUS[15] = mxA2 ? 1'b1 : 1'bz;  // Controlled_Buffer controlled_buffer_26
  assign CPSW[0] = clPSWSTART ? 1'b1 : 1'bz;  // Controlled_Buffer controlled_buffer_27
  assign CPSW[1] = ldI ? 1'b1 : 1'bz;  // Controlled_Buffer controlled_buffer_28
  assign CPSW[2] = ldV ? 1'b1 : 1'bz;  // Controlled_Buffer controlled_buffer_29
  assign CPSW[3] = ldC ? 1'b1 : 1'bz;  // Controlled_Buffer controlled_buffer_30
  assign CPSW[4] = ldN ? 1'b1 : 1'bz;  // Controlled_Buffer controlled_buffer_31
  assign CPSW[5] = ldZ ? 1'b1 : 1'bz;  // Controlled_Buffer controlled_buffer_32
  assign CPSW[6] = ldSTART ? 1'b1 : 1'bz;  // Controlled_Buffer controlled_buffer_33
  assign rdMEM = rdMEM_t ? 1'b1 : 1'bz;  // Controlled_Buffer controlled_buffer_34
  assign wrMEM = wrMEM_t ? 1'b1 : 1'bz;  // Controlled_Buffer controlled_buffer_35

  // Other names for the same wires on the sheet: A7__0[7:0] = A[7:0]; A15__0[15:0] = A; immed = ADDRBUS[0];
  //   memind = ADDRBUS[1]; regdir = ADDRBUS[2]; regind = ADDRBUS[3]; predec = ADDRBUS[4]; pcrelpom = ADDRBUS[5];
  //   ALU15__0[15:0] = ALU; B15__0[15:0] = B; CLK = in_2; cout = out_13; FCBUS = in_3; HALT = INSTRUCBUS[0];
  //   RTS = INSTRUCBUS[1]; RTI = INSTRUCBUS[2]; ROR = INSTRUCBUS[3]; PUSH = INSTRUCBUS[4]; POP = INSTRUCBUS[5];
  //   BOVF = INSTRUCBUS[6]; BNCR = INSTRUCBUS[7]; BLEQ = INSTRUCBUS[8]; BLSSU = INSTRUCBUS[9]; LD = INSTRUCBUS[10];
  //   ST = INSTRUCBUS[11]; DEC = INSTRUCBUS[12]; SUB = INSTRUCBUS[13]; XOR = INSTRUCBUS[14]; AND = INSTRUCBUS[15];
  //   STRFIND = INSTRUCBUS[16]; JLEQ = INSTRUCBUS[17]; JMP = INSTRUCBUS[18]; JSR = INSTRUCBUS[19];
  //   MAR15__0[15:0] = in_7; MDR7__0[7:0] = in_6; EXEC = PHASEFFBUS[2]; PSWSTART = PSW[0]; PSWZ = PSW[1];
  //   PSWN = PSW[2]; PSWV = PSW[3]; PSWC = PSW[4]; PSWI = PSW[15]; rst = in_1

  // Notes on the sheet:
  //   ALU
  //   Operaciona jedinica
  //   Upravljacka jedinica
  //   CMP
  //   Uslov za skok
endmodule

module INTR (
  input  in_1,
  input  in_2,
  input  in_3,
  input  [3:0] PHASEFFBUS,
  input  [19:0] INSTRUCBUS,
  input  [15:0] PSW,
  input  [7:0] intr,
  output [15:0] ADDIVTP,
  output [2:0] UEXT2__0,
  output inta,
  output [15:0] CMEMBUS,
  output [7:0] CFFBUS,
  output [15:0] CREGBUS,
  output rdMEM,
  output wrMEM
);

  wire and_2_out, and_3_out, and_4_out, brcnd, brnotFCBUS, brnotINTR, brnotprekid, bruncnd, clINTR, incMAR,
       incPC, incSP, ldDWH, ldDWL, ldINTR, ldMAR, ldMDR, ldPC, mxMAR0, mxMAR1, mxMAR2, mxMDR0, mxMDR1,
       mxMDR2, mxMDR3, not_1_out, not_2_out, not_4_out, not_5_out, not_6_out, or_1_out, prekid, rdMEM_t,
       reg5_cl_inc_ld_1_p6, reg5_cl_inc_ld_1_p7, stFETCH, wrMEM_t;
  wire [2:0] reg3_ld_1_p3;
  wire [4:0] reg5_cl_inc_ld_1_p4, reg5_cl_inc_ld_1_p5;
  wire [15:0] IVTP;
  wire [22:20] dc3_8_1_p1;

  or or_1 (or_1_out, intr[7], intr[6], intr[5], intr[4], intr[3], intr[2], intr[1], intr[0]);
  not not_1 (not_1_out, INSTRUCBUS[0]);
  // REG16_LD reg16_ld_1: pin names not known; wires that end beside it: in_2, {16{1'b0}}, IVTP, in_1
  not not_2 (not_2_out, in_1);
  and and_1 (prekid, or_1_out, PSW[15], not_1_out);
  // REG5_CL_INC_LD reg5_cl_inc_ld_1: pin names not known; wires that end beside it: 1'b0, in_2, not_2_out, reg5_cl_inc_ld_1_p4, reg5_cl_inc_ld_1_p5, reg5_cl_inc_ld_1_p6, reg5_cl_inc_ld_1_p7
  // DC3_8 dc3_8_1: pin names not known; wires that end beside it: dc3_8_1_p1, 1'b1, bruncnd, brnotINTR, brnotprekid, brnotFCBUS
  Priority_Encoder priority_encoder_1 (
    .in0(intr[0]), .in1(intr[1]), .in2(intr[2]), .in3(intr[3]), .in4(intr[4]), .in5(intr[5]), .in6(intr[6]),
    .in7(intr[7]), .out(UEXT2__0), .en_in(1'b1));  // open: gs, en_out
  or or_2 (reg5_cl_inc_ld_1_p6, bruncnd, brcnd);
  not not_3 (reg5_cl_inc_ld_1_p7, reg5_cl_inc_ld_1_p6);
  ROM32x28 rom32x28_1 (
    .A4__0(reg5_cl_inc_ld_1_p5), .CS(1'b1),
    .DOUT({reg5_cl_inc_ld_1_p4, dc3_8_1_p1, ldPC, mxMDR3, stFETCH, clINTR, incPC, ldDWL, ldDWH, incMAR, rdMEM_t, mxMAR1, mxMDR2, wrMEM_t, ldINTR, incSP, ldMDR, mxMDR0, mxMDR1, ldMAR, mxMAR2, mxMAR0}));
  // REG3_LD reg3_ld_1: pin names not known; wires that end beside it: in_2, UEXT2__0, reg3_ld_1_p3, ldINTR
  // ADD16 add16_1: pin names not known; wires that end beside it: IVTP, ADDIVTP, {{12{1'b0}}, reg3_ld_1_p3, 1'b0}
  not not_4 (not_4_out, prekid);
  and and_2 (and_2_out, not_4_out, brnotprekid);
  not not_5 (not_5_out, PHASEFFBUS[3]);
  and and_3 (and_3_out, not_5_out, brnotINTR);
  not not_6 (not_6_out, in_3);
  and and_4 (and_4_out, not_6_out, brnotFCBUS);
  or or_3 (brcnd, and_2_out, and_3_out, and_4_out);
  assign CMEMBUS[0] = ldMAR ? 1'b1 : 1'bz;  // Controlled_Buffer controlled_buffer_1
  assign CMEMBUS[1] = mxMDR3 ? 1'b1 : 1'bz;  // Controlled_Buffer controlled_buffer_2
  assign CMEMBUS[2] = ldMDR ? 1'b1 : 1'bz;  // Controlled_Buffer controlled_buffer_3
  assign CMEMBUS[3] = ldPC ? 1'b1 : 1'bz;  // Controlled_Buffer controlled_buffer_4
  assign CMEMBUS[4] = incPC ? 1'b1 : 1'bz;  // Controlled_Buffer controlled_buffer_5
  assign CMEMBUS[5] = mxMAR0 ? 1'b1 : 1'bz;  // Controlled_Buffer controlled_buffer_6
  assign CMEMBUS[6] = mxMAR1 ? 1'b1 : 1'bz;  // Controlled_Buffer controlled_buffer_7
  assign CMEMBUS[7] = mxMAR2 ? 1'b1 : 1'bz;  // Controlled_Buffer controlled_buffer_8
  assign CMEMBUS[8] = incMAR ? 1'b1 : 1'bz;  // Controlled_Buffer controlled_buffer_9
  assign CMEMBUS[9] = mxMDR0 ? 1'b1 : 1'bz;  // Controlled_Buffer controlled_buffer_10
  assign CMEMBUS[10] = mxMDR1 ? 1'b1 : 1'bz;  // Controlled_Buffer controlled_buffer_11
  assign CMEMBUS[11] = mxMDR2 ? 1'b1 : 1'bz;  // Controlled_Buffer controlled_buffer_12
  assign CMEMBUS[12] = incSP ? 1'b1 : 1'bz;  // Controlled_Buffer controlled_buffer_13
  assign CREGBUS[10] = ldDWL ? 1'b1 : 1'bz;  // Controlled_Buffer controlled_buffer_14
  assign CREGBUS[11] = ldDWH ? 1'b1 : 1'bz;  // Controlled_Buffer controlled_buffer_15
  assign CFFBUS[0] = stFETCH ? 1'b1 : 1'bz;  // Controlled_Buffer controlled_buffer_16
  assign CFFBUS[7] = clINTR ? 1'b1 : 1'bz;  // Controlled_Buffer controlled_buffer_17
  assign rdMEM = rdMEM_t ? 1'b1 : 1'bz;  // Controlled_Buffer controlled_buffer_18
  assign wrMEM = wrMEM_t ? 1'b1 : 1'bz;  // Controlled_Buffer controlled_buffer_19
  or or_4 (inta, ldINTR, in_1);

  // Other names for the same wires on the sheet: ADDIVTP15__0[15:0] = ADDIVTP; CLK = in_2; FCBUS = in_3;
  //   HALT = INSTRUCBUS[0]; intr7__0[7:0] = intr; INTR_t = PHASEFFBUS[3]; PSWI = PSW[15]; rst = in_1

  // Notes on the sheet:
  //   Operaciona jedinica
  //   Upravljacka jedinica
endmodule

module RAM (
  input  [15:0] in_1,
  input  in_2,
  input  [7:0] in_3,
  input  in_4,
  input  in_5,
  input  in_6,
  output [7:0] out_7,
  output out_8
);

  wire and_1_out, and_2_out, CNT0, LDCNT, not_1_out, notCNT0, or_1_out, reg4_ld_sl_sr_1_p6, rsff_2_p4,
       rsff_2_p5, rsff_3_p4, sl;
  wire [3:0] CNT, LFSR;

  // RSFF rsff_1: pin names not known; wires that end beside it: 1'b0, in_2, in_6, sl
  or or_1 (or_1_out, in_4, in_5);
  // REG4_LD_SL_SR reg4_ld_sl_sr_1: pin names not known; wires that end beside it: 1'b0, 1'b0, in_2, 4'b1111, LFSR, reg4_ld_sl_sr_1_p6, sl, in_6
  // RisingEdge risingedge_1: pin names not known; wires that end beside it: or_1_out, in_2, LDCNT
  // MEM64Kx8 mem64kx8_1: pin names not known; wires that end beside it: in_1, 1'b1, in_2, in_3, out_7, in_4
  xor xor_1 (reg4_ld_sl_sr_1_p6, LFSR[2], LFSR[3]);
  and and_1 (and_1_out, CNT0, not_1_out);
  not not_1 (not_1_out, LDCNT);
  // RSFF rsff_2: pin names not known; wires that end beside it: and_1_out, in_2, LDCNT, rsff_2_p4, rsff_2_p5
  not not_2 (rsff_2_p4, in_6);
  and and_2 (and_2_out, rsff_2_p5, CNT0);
  // REG4m_DEC_LD reg4m_dec_ld_1: pin names not known; wires that end beside it: in_2, LFSR, CNT, LDCNT, notCNT0, notCNT0
  or or_2 (notCNT0, CNT[0], CNT[1], CNT[2], CNT[3]);
  // RSFF rsff_3: pin names not known; wires that end beside it: out_8, in_2, and_2_out, rsff_3_p4, out_8
  not not_3 (rsff_3_p4, in_6);
  not not_4 (CNT0, notCNT0);

  // Other names for the same wires on the sheet: ADR[15:0] = in_1; CLK = in_2; DIN[7:0] = in_3; DOUT[7:0] = out_7;
  //   fc = out_8; RDMEM = in_5; rst = in_6; WRMEM = in_4

  // Notes on the sheet:
  //   Random broj predstavlja vreme pristupa memoriji
  //   Brojac za generisanje random broja 
  //   Jedinica za generisanje function complete (fc) signala
  //   Brojac za dekrementiranje random broja
endmodule
